// Logisim project 6.circ as structural Verilog: 1 circuit, main circuit main
module main (
  input  a,
  input  b,
  input  c,
  output x,
  output y
);

  wire xor_1_out;

  xor xor_1 (xor_1_out, a, b);
  xor xor_2 (x, xor_1_out, c);
  and and_1 (y, xor_1_out, c);
endmodule
