// Logisim project 7_3.circ as structural Verilog: 1 circuit, main circuit main
module main (
  input  a,
  input  b,
  input  c,
  input  d,
  input  e,
  output x,
  output y,
  output z
);

  wire and_1_out, and_2_out, and_3_out, and_4_out, and_5_out, and_6_out, and_7_out, and_8_out, and_9_out,
       not_1_out, not_2_out, not_3_out, not_4_out, not_5_out, not_6_out, not_7_out, not_8_out, not_9_out,
       not_10_out, not_11_out;

  not not_1 (not_1_out, b);
  not not_2 (not_2_out, a);
  not not_3 (not_3_out, c);
  not not_4 (not_4_out, a);
  not not_5 (not_5_out, b);
  not not_6 (not_6_out, a);
  not not_7 (not_7_out, e);
  not not_8 (not_8_out, d);
  not not_9 (not_9_out, b);
  not not_10 (not_10_out, d);
  not not_11 (not_11_out, c);
  and and_1 (and_1_out, not_1_out, c);
  and and_2 (and_2_out, a, b);
  and and_3 (and_3_out, not_2_out, not_3_out);
  and and_4 (and_4_out, not_4_out, b);
  and and_5 (and_5_out, a, not_5_out);
  and and_6 (and_6_out, not_6_out, b, not_7_out);
  and and_7 (and_7_out, b, not_8_out, e);
  and and_8 (and_8_out, a, not_9_out, not_10_out);
  and and_9 (and_9_out, a, b, not_11_out, e);
  or or_1 (x, and_1_out, and_2_out);
  or or_2 (y, and_3_out, and_4_out, and_5_out);
  or or_3 (z, and_6_out, and_7_out, and_8_out, and_9_out);
endmodule
