// Logisim project 1.circ as structural Verilog: 1 circuit, main circuit main
module main (
  input  P,
  input  C,
  input  R,
  input  E,
  input  S,
  output X,
  output Y
);

  wire A1_out, A4_out, N1_out, N2_out, O1_out, O2_out, O3_out, O4_out;

  not N1 (N1_out, C);
  and A4 (A4_out, P, C);
  or O4 (O4_out, P, S);
  or O1 (O1_out, N1_out, R);
  or O2 (O2_out, E, S);
  or O3 (O3_out, R, A4_out);
  and A1 (A1_out, O4_out, O1_out);
  not N2 (N2_out, E);
  and A2 (X, A1_out, N2_out);
  and A3 (Y, O2_out, O3_out);
endmodule
